// Logisim project CPU.circ as structural Verilog: 9 circuits, main circuit CPU
module CPU (
);

  wire and_1_out, Clock_out, control_unit_1_alusrc, control_unit_1_branch, control_unit_1_jump,
       control_unit_1_memread, control_unit_1_memtoreg, control_unit_1_memwrite, control_unit_1_regwrite,
       control_unit_1_reqdst, n16_bit_alu_1_zero, not_1_out;
  wire [3:0] control_unit_1_aluop;
  wire [4:0] instruction_fetch_1_rd, instruction_fetch_1_rs, instruction_fetch_1_rt, multiplexer_1_out;
  wire [5:0] instruction_fetch_1_opcode;
  wire [15:0] instruction_fetch_1_offset, multiplexer_2_out, multiplexer_3_out, multiplexer_4_out,
       multiplexer_5_out, n16_bit_adder_1_sum, n16_bit_alu_1_out_5, PC_q, ram_2_data, register_1_out_7,
       register_1_out_8;
  wire [31:0] ram_1_data;

  Clock Clock (.out(Clock_out));
  Register #(.width(16)) PC (.D(multiplexer_5_out), .en(1'b1), .Q(PC_q), .clk(Clock_out));  // open: clr
  _16___Bit_Adder u_16_bit_adder_1 (.A(16'h1), .B(PC_q), .SUM(n16_bit_adder_1_sum));  // open: Overflow
  RAM #(.addrWidth(16), .dataWidth(32)) ram_1 (.addr(PC_q), .data(ram_1_data), .clk(Clock_out));  // open: sel, ld, clr
  Instruction_Fetch instruction_fetch_1 (
    .in_1(ram_1_data), .opcode(instruction_fetch_1_opcode), .rs(instruction_fetch_1_rs),
    .rt(instruction_fetch_1_rt), .rd(instruction_fetch_1_rd), .offset(instruction_fetch_1_offset));
  Multiplexer #(.width(5)) multiplexer_1 (
    .in0(instruction_fetch_1_rt), .in1(instruction_fetch_1_rd), .out(multiplexer_1_out),
    .sel(control_unit_1_reqdst));  // open: en
  register register_1 (
    .read_register_1(instruction_fetch_1_rs), .read_register_2(instruction_fetch_1_rt),
    .write_register(multiplexer_1_out), .write_data(multiplexer_4_out), .RegWrite(control_unit_1_regwrite),
    .in_6(Clock_out), .out_7(register_1_out_7), .out_8(register_1_out_8));
  Control_Unit control_unit_1 (
    .opcode(instruction_fetch_1_opcode), .branch(control_unit_1_branch), .MemToReg(control_unit_1_memtoreg),
    .MemRead(control_unit_1_memread), .MemWrite(control_unit_1_memwrite), .ALUsrc(control_unit_1_alusrc),
    .RegWrite(control_unit_1_regwrite), .ALUop(control_unit_1_aluop), .ReqDst(control_unit_1_reqdst),
    .jump(control_unit_1_jump));
  Multiplexer #(.width(16)) multiplexer_2 (
    .in0(register_1_out_8), .in1(instruction_fetch_1_offset), .out(multiplexer_2_out),
    .sel(control_unit_1_alusrc));  // open: en
  _16_Bit_ALU u_16_bit_alu_1 (
    .A(register_1_out_7), .B(multiplexer_2_out), .operation(control_unit_1_aluop),
    .out_5(n16_bit_alu_1_out_5), .in_4(Clock_out), .Zero(n16_bit_alu_1_zero));
  and and_1 (and_1_out, control_unit_1_branch, n16_bit_alu_1_zero);
  Multiplexer #(.width(16)) multiplexer_3 (
    .in0(n16_bit_adder_1_sum), .in1(instruction_fetch_1_offset), .out(multiplexer_3_out), .sel(and_1_out));  // open: en
  RAM #(.addrWidth(16), .dataWidth(16), .bus("separate")) ram_2 (
    .addr(n16_bit_alu_1_out_5), .din(register_1_out_8), .data(ram_2_data), .str(control_unit_1_memwrite),
    .clk(Clock_out), .ld(control_unit_1_memread));  // open: sel, clr
  Multiplexer #(.width(16)) multiplexer_4 (
    .in0(n16_bit_alu_1_out_5), .in1(ram_2_data), .out(multiplexer_4_out), .sel(control_unit_1_memtoreg));  // open: en
  Multiplexer #(.width(16)) multiplexer_5 (
    .in0(instruction_fetch_1_offset), .in1(multiplexer_3_out), .out(multiplexer_5_out), .sel(not_1_out));  // open: en
  not not_1 (not_1_out, control_unit_1_jump);

  // Notes on the sheet:
  //   Instruction Memory
  //   Data Memory
endmodule

// ALU
module _16_Bit_ALU (
  input  [15:0] A,
  input  [15:0] B,
  input  [3:0] operation,
  input  in_4,
  output [15:0] out_5,
  output Zero
);

  wire comparator_1_eq, comparator_2_eq, comparator_3_gt, not_1_out;
  wire [15:0] and_out, divider_1_rem, mfhi, mflo, MultHi, MultLo, n16_bit_adder_1_sum, n16_bit_adder_2_sum,
       or_out, shifter_1_out, slt_1_output, subtractor_1_out;

  Comparator #(.width(4)) comparator_1 (.a(operation), .b(4'b0010), .eq(comparator_1_eq));  // open: gt, lt
  _16___Bit_Adder u_16_bit_adder_1 (.A(A), .B(B), .SUM(n16_bit_adder_1_sum));  // open: Overflow
  Subtractor #(.width(16)) subtractor_1 (.a(A), .b(B), .out(subtractor_1_out));  // open: bin, bout
  signed_multiplier signed_multiplier_1 (.in_1(A), .in_2(B), .lo(MultLo), .hi(MultHi));
  assign and_out = A & B;  // AND_Gate and, 16 bits wide
  assign or_out = A | B;  // OR_Gate or, 16 bits wide
  _16___Bit_Adder u_16_bit_adder_2 (.A(B), .B(A), .SUM(n16_bit_adder_2_sum));  // open: Overflow
  slt slt_1 (.rs(A), .rt(B), .Output(slt_1_output));
  Shifter #(.width(16)) shifter_1 (.in(A), .\dist (B[3:0]), .out(shifter_1_out));
  Divider #(.width(16)) divider_1 (.a(A), .b(B), .rem(divider_1_rem));  // open: out, upper
  Register #(.width(16)) u_MultHi (.D(MultHi), .en(comparator_1_eq), .Q(mfhi), .clk(in_4));  // open: clr
  Register #(.width(16)) u_MultLo (.D(MultLo), .en(comparator_1_eq), .Q(mflo), .clk(in_4));  // open: clr
  Comparator #(.width(16)) comparator_2 (.a(A), .b(B), .eq(comparator_2_eq));  // open: gt, lt
  Comparator #(.width(16)) comparator_3 (.a(A), .b({16{1'b0}}), .gt(comparator_3_gt));  // open: eq, lt
  not not_1 (not_1_out, comparator_3_gt);
  Multiplexer #(.select(4), .width(16)) multiplexer_1 (
    .in0(n16_bit_adder_1_sum), .in1(subtractor_1_out), .in3(and_out), .in4(or_out),
    .in5(n16_bit_adder_2_sum), .in6(shifter_1_out), .in7(slt_1_output), .in8(mfhi), .in9(mflo),
    .in10(n16_bit_adder_1_sum), .in11(n16_bit_adder_1_sum), .in15(divider_1_rem), .out(out_5), .sel(operation));  // open: in2, in12, in13, in14, en
  Multiplexer #(.select(4)) multiplexer_2 (
    .in0(1'b0), .in1(1'b0), .in2(1'b0), .in3(1'b0), .in4(1'b0), .in5(1'b0), .in6(1'b0), .in7(1'b0),
    .in8(1'b0), .in9(1'b0), .in10(1'b0), .in11(1'b0), .in12(comparator_2_eq), .in13(not_1_out), .in14(1'b0),
    .in15(1'b0), .out(Zero), .sel(operation));  // open: en

  // Other names for the same wires on the sheet: Op[3:0] = operation
endmodule

module Control_Unit (
  input  [5:0] opcode,
  output ReqDst,
  output RegWrite,
  output ALUsrc,
  output MemWrite,
  output MemRead,
  output MemToReg,
  output branch,
  output jump,
  output [3:0] ALUop
);

  Multiplexer #(.select(4), .width(8)) multiplexer_1 (
    .in0(8'h3), .in1(8'h3), .in2(8'h1), .in3(8'h3), .in4(8'h3), .in5(8'h6), .in6(8'h6), .in7(8'h3),
    .in8(8'h3), .in9(8'h3), .in10(8'h36), .in11(8'hc), .in12(8'h40), .in13(8'h44), .in14(8'h80), .in15(8'h3),
    .out({jump, branch, MemToReg, MemRead, MemWrite, ALUsrc, RegWrite, ReqDst}), .sel(opcode[3:0]));  // open: en

  assign ALUop = opcode[3:0];
endmodule

// fetch
module Instruction_Fetch (
  input  [31:0] in_1,
  output [4:0] rd,
  output [15:0] offset,
  output [4:0] rt,
  output [4:0] rs,
  output [5:0] opcode
);


  assign offset = in_1[15:0];
  assign opcode = in_1[31:26];
  assign rd = in_1[15:11];
  assign rs = in_1[25:21];
  assign rt = in_1[20:16];
endmodule

module slt (
  input  [15:0] rs,
  input  [15:0] rt,
  output [15:0] Output
);

  wire [15:0] subtractor_1_out;

  Subtractor #(.width(16)) subtractor_1 (.a(rs), .b(rt), .out(subtractor_1_out));  // open: bin, bout
  Multiplexer #(.width(16)) multiplexer_1 (
    .in0({16{1'b0}}), .in1(16'h1), .out(Output), .sel(subtractor_1_out[15]));  // open: en
endmodule

// +1
module _1_Bit_Adder (
  input  A,
  input  B,
  input  Cin,
  output Sum,
  output Cout
);

  wire and_2_out, and_out, Xor_out;

  xor Xor (Xor_out, A, B);
  xor Xor_2 (Sum, Xor_out, Cin);
  and \and  (and_out, Cin, Xor_out);
  and and_2 (and_2_out, A, B);
  or \or  (Cout, and_out, and_2_out);
endmodule

// add
module _16___Bit_Adder (
  input  [15:0] A,
  input  [15:0] B,
  output [15:0] SUM,
  output Overflow
);

  wire n1_bit_adder_1_cout, n1_bit_adder_2_cout, n1_bit_adder_3_cout, n1_bit_adder_4_cout,
       n1_bit_adder_5_cout, n1_bit_adder_6_cout, n1_bit_adder_7_cout, n1_bit_adder_8_cout,
       n1_bit_adder_9_cout, n1_bit_adder_10_cout, n1_bit_adder_11_cout, n1_bit_adder_12_cout,
       n1_bit_adder_13_cout, n1_bit_adder_14_cout, n1_bit_adder_15_cout;

  _1_Bit_Adder u_1_bit_adder_1 (.A(A[0]), .B(B[0]), .Cin(1'b0), .Sum(SUM[0]), .Cout(n1_bit_adder_1_cout));
  _1_Bit_Adder u_1_bit_adder_2 (
    .A(A[1]), .B(B[1]), .Cin(n1_bit_adder_1_cout), .Sum(SUM[1]), .Cout(n1_bit_adder_2_cout));
  _1_Bit_Adder u_1_bit_adder_3 (
    .A(A[2]), .B(B[2]), .Cin(n1_bit_adder_2_cout), .Sum(SUM[2]), .Cout(n1_bit_adder_3_cout));
  _1_Bit_Adder u_1_bit_adder_4 (
    .A(A[3]), .B(B[3]), .Cin(n1_bit_adder_3_cout), .Sum(SUM[3]), .Cout(n1_bit_adder_4_cout));
  _1_Bit_Adder u_1_bit_adder_5 (
    .A(A[4]), .B(B[4]), .Cin(n1_bit_adder_4_cout), .Sum(SUM[4]), .Cout(n1_bit_adder_5_cout));
  _1_Bit_Adder u_1_bit_adder_6 (
    .A(A[5]), .B(B[5]), .Cin(n1_bit_adder_5_cout), .Sum(SUM[5]), .Cout(n1_bit_adder_6_cout));
  _1_Bit_Adder u_1_bit_adder_7 (
    .A(A[6]), .B(B[6]), .Cin(n1_bit_adder_6_cout), .Sum(SUM[6]), .Cout(n1_bit_adder_7_cout));
  _1_Bit_Adder u_1_bit_adder_8 (
    .A(A[7]), .B(B[7]), .Cin(n1_bit_adder_7_cout), .Sum(SUM[7]), .Cout(n1_bit_adder_8_cout));
  _1_Bit_Adder u_1_bit_adder_9 (
    .A(A[8]), .B(B[8]), .Cin(n1_bit_adder_8_cout), .Sum(SUM[8]), .Cout(n1_bit_adder_9_cout));
  _1_Bit_Adder u_1_bit_adder_10 (
    .A(A[9]), .B(B[9]), .Cin(n1_bit_adder_9_cout), .Sum(SUM[9]), .Cout(n1_bit_adder_10_cout));
  _1_Bit_Adder u_1_bit_adder_11 (
    .A(A[10]), .B(B[10]), .Cin(n1_bit_adder_10_cout), .Sum(SUM[10]), .Cout(n1_bit_adder_11_cout));
  _1_Bit_Adder u_1_bit_adder_12 (
    .A(A[11]), .B(B[11]), .Cin(n1_bit_adder_11_cout), .Sum(SUM[11]), .Cout(n1_bit_adder_12_cout));
  _1_Bit_Adder u_1_bit_adder_13 (
    .A(A[12]), .B(B[12]), .Cin(n1_bit_adder_12_cout), .Sum(SUM[12]), .Cout(n1_bit_adder_13_cout));
  _1_Bit_Adder u_1_bit_adder_14 (
    .A(A[13]), .B(B[13]), .Cin(n1_bit_adder_13_cout), .Sum(SUM[13]), .Cout(n1_bit_adder_14_cout));
  _1_Bit_Adder u_1_bit_adder_15 (
    .A(A[14]), .B(B[14]), .Cin(n1_bit_adder_14_cout), .Sum(SUM[14]), .Cout(n1_bit_adder_15_cout));
  _1_Bit_Adder u_1_bit_adder_16 (.A(A[15]), .B(B[15]), .Cin(n1_bit_adder_15_cout), .Sum(SUM[15]), .Cout(Overflow));
endmodule

// Register File
module register (
  input  [4:0] read_register_1,
  input  [4:0] read_register_2,
  input  [4:0] write_register,
  input  [15:0] write_data,
  input  RegWrite,
  input  in_6,
  output [15:0] out_7,
  output [15:0] out_8
);

  wire and_1_out, and_2_out, and_3_out, and_4_out, and_5_out, and_6_out, and_7_out, and_8_out, and_9_out,
       and_10_out, and_11_out, and_12_out, and_13_out, and_14_out, and_15_out, and_16_out, and_17_out,
       and_18_out, and_19_out, and_20_out, and_21_out, and_22_out, and_23_out, and_24_out, and_25_out,
       and_26_out, and_27_out, and_28_out, and_29_out, and_30_out, and_31_out, and_32_out, decoder_1_out0,
       decoder_1_out1, decoder_1_out2, decoder_1_out3, decoder_1_out4, decoder_1_out5, decoder_1_out6,
       decoder_1_out7, decoder_1_out8, decoder_1_out9, decoder_1_out10, decoder_1_out11, decoder_1_out12,
       decoder_1_out13, decoder_1_out14, decoder_1_out15, decoder_1_out16, decoder_1_out17, decoder_1_out18,
       decoder_1_out19, decoder_1_out20, decoder_1_out21, decoder_1_out22, decoder_1_out23, decoder_1_out24,
       decoder_1_out25, decoder_1_out26, decoder_1_out27, decoder_1_out28, decoder_1_out29, decoder_1_out30,
       decoder_1_out31;
  wire [15:0] register_1_q, register_2_q, register_3_q, register_4_q, register_5_q, register_6_q,
       register_7_q, register_8_q, register_9_q, register_10_q, register_11_q, register_12_q, register_13_q,
       register_14_q, register_15_q, register_16_q, register_17_q, register_18_q, register_19_q,
       register_20_q, register_21_q, register_22_q, register_23_q, register_24_q, register_25_q,
       register_26_q, register_27_q, register_28_q, register_29_q, register_30_q, register_31_q,
       register_32_q;

  Decoder #(.select(5)) decoder_1 (
    .out0(decoder_1_out0), .out1(decoder_1_out1), .out2(decoder_1_out2), .out3(decoder_1_out3),
    .out4(decoder_1_out4), .out5(decoder_1_out5), .out6(decoder_1_out6), .out7(decoder_1_out7),
    .out8(decoder_1_out8), .out9(decoder_1_out9), .out10(decoder_1_out10), .out11(decoder_1_out11),
    .out12(decoder_1_out12), .out13(decoder_1_out13), .out14(decoder_1_out14), .out15(decoder_1_out15),
    .out16(decoder_1_out16), .out17(decoder_1_out17), .out18(decoder_1_out18), .out19(decoder_1_out19),
    .out20(decoder_1_out20), .out21(decoder_1_out21), .out22(decoder_1_out22), .out23(decoder_1_out23),
    .out24(decoder_1_out24), .out25(decoder_1_out25), .out26(decoder_1_out26), .out27(decoder_1_out27),
    .out28(decoder_1_out28), .out29(decoder_1_out29), .out30(decoder_1_out30), .out31(decoder_1_out31),
    .sel(write_register));  // open: en
  and and_1 (and_1_out, decoder_1_out0, RegWrite);
  and and_2 (and_2_out, decoder_1_out1, RegWrite);
  and and_3 (and_3_out, decoder_1_out2, RegWrite);
  and and_4 (and_4_out, decoder_1_out3, RegWrite);
  and and_5 (and_5_out, decoder_1_out4, RegWrite);
  and and_6 (and_6_out, decoder_1_out5, RegWrite);
  and and_7 (and_7_out, decoder_1_out6, RegWrite);
  and and_8 (and_8_out, decoder_1_out7, RegWrite);
  Register #(.width(16)) register_1 (.D(write_data), .en(and_1_out), .Q(register_1_q), .clk(in_6), .clr(1'b1));
  Register #(.width(16)) register_2 (.D(write_data), .en(and_2_out), .Q(register_2_q), .clk(in_6));  // open: clr
  Register #(.width(16)) register_3 (.D(write_data), .en(and_3_out), .Q(register_3_q), .clk(in_6));  // open: clr
  Register #(.width(16)) register_4 (.D(write_data), .en(and_4_out), .Q(register_4_q), .clk(in_6));  // open: clr
  Register #(.width(16)) register_5 (.D(write_data), .en(and_5_out), .Q(register_5_q), .clk(in_6));  // open: clr
  Register #(.width(16)) register_6 (.D(write_data), .en(and_6_out), .Q(register_6_q), .clk(in_6));  // open: clr
  Register #(.width(16)) register_7 (.D(write_data), .en(and_7_out), .Q(register_7_q), .clk(in_6));  // open: clr
  Register #(.width(16)) register_8 (.D(write_data), .en(and_8_out), .Q(register_8_q), .clk(in_6));  // open: clr
  and and_9 (and_9_out, decoder_1_out8, RegWrite);
  and and_10 (and_10_out, decoder_1_out9, RegWrite);
  and and_11 (and_11_out, decoder_1_out10, RegWrite);
  and and_12 (and_12_out, decoder_1_out11, RegWrite);
  and and_13 (and_13_out, decoder_1_out12, RegWrite);
  and and_14 (and_14_out, decoder_1_out13, RegWrite);
  and and_15 (and_15_out, decoder_1_out14, RegWrite);
  and and_16 (and_16_out, decoder_1_out15, RegWrite);
  Register #(.width(16)) register_9 (.D(write_data), .en(and_9_out), .Q(register_9_q), .clk(in_6));  // open: clr
  Register #(.width(16)) register_10 (.D(write_data), .en(and_10_out), .Q(register_10_q), .clk(in_6));  // open: clr
  Register #(.width(16)) register_11 (.D(write_data), .en(and_11_out), .Q(register_11_q), .clk(in_6));  // open: clr
  Register #(.width(16)) register_12 (.D(write_data), .en(and_12_out), .Q(register_12_q), .clk(in_6));  // open: clr
  Register #(.width(16)) register_13 (.D(write_data), .en(and_13_out), .Q(register_13_q), .clk(in_6));  // open: clr
  Register #(.width(16)) register_14 (.D(write_data), .en(and_14_out), .Q(register_14_q), .clk(in_6));  // open: clr
  Register #(.width(16)) register_15 (.D(write_data), .en(and_15_out), .Q(register_15_q), .clk(in_6));  // open: clr
  Register #(.width(16)) register_16 (.D(write_data), .en(and_16_out), .Q(register_16_q), .clk(in_6));  // open: clr
  and and_17 (and_17_out, decoder_1_out16, RegWrite);
  and and_18 (and_18_out, decoder_1_out17, RegWrite);
  and and_19 (and_19_out, decoder_1_out18, RegWrite);
  and and_20 (and_20_out, decoder_1_out19, RegWrite);
  and and_21 (and_21_out, decoder_1_out20, RegWrite);
  and and_22 (and_22_out, decoder_1_out21, RegWrite);
  and and_23 (and_23_out, decoder_1_out22, RegWrite);
  and and_24 (and_24_out, decoder_1_out23, RegWrite);
  Register #(.width(16)) register_17 (.D(write_data), .en(and_17_out), .Q(register_17_q), .clk(in_6));  // open: clr
  Register #(.width(16)) register_18 (.D(write_data), .en(and_18_out), .Q(register_18_q), .clk(in_6));  // open: clr
  Register #(.width(16)) register_19 (.D(write_data), .en(and_19_out), .Q(register_19_q), .clk(in_6));  // open: clr
  Register #(.width(16)) register_20 (.D(write_data), .en(and_20_out), .Q(register_20_q), .clk(in_6));  // open: clr
  Register #(.width(16)) register_21 (.D(write_data), .en(and_21_out), .Q(register_21_q), .clk(in_6));  // open: clr
  Register #(.width(16)) register_22 (.D(write_data), .en(and_22_out), .Q(register_22_q), .clk(in_6));  // open: clr
  Register #(.width(16)) register_23 (.D(write_data), .en(and_23_out), .Q(register_23_q), .clk(in_6));  // open: clr
  Register #(.width(16)) register_24 (.D(write_data), .en(and_24_out), .Q(register_24_q), .clk(in_6));  // open: clr
  and and_25 (and_25_out, decoder_1_out24, RegWrite);
  and and_26 (and_26_out, decoder_1_out25, RegWrite);
  and and_27 (and_27_out, decoder_1_out26, RegWrite);
  and and_28 (and_28_out, decoder_1_out27, RegWrite);
  and and_29 (and_29_out, decoder_1_out28, RegWrite);
  and and_30 (and_30_out, decoder_1_out29, RegWrite);
  and and_31 (and_31_out, decoder_1_out30, RegWrite);
  and and_32 (and_32_out, decoder_1_out31, RegWrite);
  Register #(.width(16)) register_25 (.en(and_25_out), .Q(register_25_q), .clk(in_6));  // open: D, clr
  Register #(.width(16)) register_26 (.D(write_data), .en(and_26_out), .Q(register_26_q), .clk(in_6));  // open: clr
  Register #(.width(16)) register_27 (.D(write_data), .en(and_27_out), .Q(register_27_q), .clk(in_6));  // open: clr
  Register #(.width(16)) register_28 (.D(write_data), .en(and_28_out), .Q(register_28_q), .clk(in_6));  // open: clr
  Register #(.width(16)) register_29 (.D(write_data), .en(and_29_out), .Q(register_29_q), .clk(in_6));  // open: clr
  Register #(.width(16)) register_30 (.D(write_data), .en(and_30_out), .Q(register_30_q), .clk(in_6));  // open: clr
  Register #(.width(16)) register_31 (.D(write_data), .en(and_31_out), .Q(register_31_q), .clk(in_6));  // open: clr
  Register #(.width(16)) register_32 (.D(write_data), .en(and_32_out), .Q(register_32_q), .clk(in_6));  // open: clr
  Multiplexer #(.select(5), .width(16)) multiplexer_1 (
    .in0(register_1_q), .in1(register_2_q), .in2(register_3_q), .in3(register_4_q), .in4(register_5_q),
    .in5(register_6_q), .in6(register_7_q), .in7(register_8_q), .in8(register_9_q), .in9(register_10_q),
    .in10(register_11_q), .in11(register_12_q), .in12(register_13_q), .in13(register_14_q),
    .in14(register_15_q), .in15(register_16_q), .in16(register_17_q), .in17(register_18_q),
    .in18(register_19_q), .in19(register_20_q), .in20(register_21_q), .in21(register_22_q),
    .in22(register_23_q), .in23(register_24_q), .in24(register_25_q), .in25(register_26_q),
    .in26(register_27_q), .in27(register_28_q), .in28(register_29_q), .in29(register_30_q),
    .in30(register_31_q), .in31(register_32_q), .out(out_7), .sel(read_register_1));  // open: en
  Multiplexer #(.select(5), .width(16)) multiplexer_2 (
    .in0(register_1_q), .in1(register_2_q), .in2(register_3_q), .in3(register_4_q), .in4(register_5_q),
    .in5(register_6_q), .in6(register_7_q), .in7(register_8_q), .in8(register_9_q), .in9(register_10_q),
    .in10(register_11_q), .in11(register_12_q), .in12(register_13_q), .in13(register_14_q),
    .in14(register_15_q), .in15(register_16_q), .in16(register_17_q), .in17(register_18_q),
    .in18(register_19_q), .in19(register_20_q), .in20(register_21_q), .in21(register_22_q),
    .in22(register_23_q), .in23(register_24_q), .in24(register_25_q), .in25(register_26_q),
    .in26(register_27_q), .in27(register_28_q), .in28(register_29_q), .in29(register_30_q),
    .in30(register_31_q), .in31(register_32_q), .out(out_8), .sel(read_register_2));  // open: en
endmodule

module signed_multiplier (
  input  [15:0] in_1,
  input  [15:0] in_2,
  output [15:0] lo,
  output [15:0] hi
);

  wire xor_1_out;
  wire [15:0] multiplexer_1_out, multiplexer_2_out, multiplier_1_cout, multiplier_1_out, negator_1_out,
       negator_2_out;
  wire [31:0] negator_3_out;

  Negator #(.width(16)) negator_1 (.in(in_1), .out(negator_1_out));
  Negator #(.width(16)) negator_2 (.in(in_2), .out(negator_2_out));
  Multiplexer #(.width(16)) multiplexer_1 (
    .in0(in_1), .in1(negator_1_out), .out(multiplexer_1_out), .sel(in_1[15]));  // open: en
  Multiplexer #(.width(16)) multiplexer_2 (
    .in0(in_2), .in1(negator_2_out), .out(multiplexer_2_out), .sel(in_2[15]));  // open: en
  Multiplier #(.width(16)) multiplier_1 (
    .a(multiplexer_1_out), .b(multiplexer_2_out), .out(multiplier_1_out), .cout(multiplier_1_cout));  // open: cin
  Negator #(.width(32)) negator_3 (.in({multiplier_1_cout, multiplier_1_out}), .out(negator_3_out));
  Multiplexer #(.width(32)) multiplexer_3 (
    .in0({multiplier_1_cout, multiplier_1_out}), .in1(negator_3_out), .out({hi, lo}), .sel(xor_1_out));  // open: en
  xor xor_1 (xor_1_out, in_1[15], in_2[15]);

  // Other names for the same wires on the sheet: A[15:0] = in_1; A_Sign = in_1[15]; B[15:0] = in_2; B_Sign = in_2[15]
endmodule
